// Logisim project regfile.circ as structural Verilog: 1 circuit, main circuit regfile
module regfile (
  input  [4:0] rs1,
  input  [4:0] rs2,
  input  [4:0] rd,
  input  [31:0] Write_Data,
  input  RegWEn,
  input  clk,
  output [31:0] ra,
  output [31:0] sp,
  output [31:0] t0,
  output [31:0] t1,
  output [31:0] t2,
  output [31:0] s0,
  output [31:0] s1,
  output [31:0] a0,
  output [31:0] Read_Data_1,
  output [31:0] Read_Data_2
);

  wire [31:0] x1, x2, x3, x4, x5, x6, x7, x8, x9, x10, x11, x12, x13, x14, x15, x16, x17, x18, x19, x20, x21,
       x22, x23, x24, x25, x26, x27, x28, x29, x30, x31;

  Register #(.width(32)) register_1 (.clk(clk), .Q(x8));  // open: D, en, clr
  Register #(.width(32)) register_2 (.clk(clk), .Q(x16));  // open: D, en, clr
  Register #(.width(32)) register_3 (.clk(clk), .Q(x24));  // open: D, en, clr
  Register #(.width(32)) register_4 (.clk(clk), .Q(x1));  // open: D, en, clr
  Register #(.width(32)) register_5 (.clk(clk), .Q(x9));  // open: D, en, clr
  Register #(.width(32)) register_6 (.clk(clk), .Q(x17));  // open: D, en, clr
  Register #(.width(32)) register_7 (.clk(clk), .Q(x25));  // open: D, en, clr
  Register #(.width(32)) register_8 (.clk(clk), .Q(x2));  // open: D, en, clr
  Register #(.width(32)) register_9 (.clk(clk), .Q(x10));  // open: D, en, clr
  Register #(.width(32)) register_10 (.clk(clk), .Q(x18));  // open: D, en, clr
  Register #(.width(32)) register_11 (.clk(clk), .Q(x26));  // open: D, en, clr
  Register #(.width(32)) register_12 (.clk(clk), .Q(x3));  // open: D, en, clr
  Register #(.width(32)) register_13 (.clk(clk), .Q(x11));  // open: D, en, clr
  Register #(.width(32)) register_14 (.clk(clk), .Q(x19));  // open: D, en, clr
  Register #(.width(32)) register_15 (.clk(clk), .Q(x27));  // open: D, en, clr
  Register #(.width(32)) register_16 (.clk(clk), .Q(x4));  // open: D, en, clr
  Register #(.width(32)) register_17 (.clk(clk), .Q(x12));  // open: D, en, clr
  Register #(.width(32)) register_18 (.clk(clk), .Q(x20));  // open: D, en, clr
  Register #(.width(32)) register_19 (.clk(clk), .Q(x28));  // open: D, en, clr
  Register #(.width(32)) register_20 (.clk(clk), .Q(x5));  // open: D, en, clr
  Register #(.width(32)) register_21 (.clk(clk), .Q(x13));  // open: D, en, clr
  Register #(.width(32)) register_22 (.clk(clk), .Q(x21));  // open: D, en, clr
  Register #(.width(32)) register_23 (.clk(clk), .Q(x29));  // open: D, en, clr
  Register #(.width(32)) register_24 (.clk(clk), .Q(x6));  // open: D, en, clr
  Register #(.width(32)) register_25 (.clk(clk), .Q(x14));  // open: D, en, clr
  Register #(.width(32)) register_26 (.clk(clk), .Q(x22));  // open: D, en, clr
  Register #(.width(32)) register_27 (.clk(clk), .Q(x30));  // open: D, en, clr
  Register #(.width(32)) register_28 (.clk(clk), .Q(x7));  // open: D, en, clr
  Register #(.width(32)) register_29 (.clk(clk), .Q(x15));  // open: D, en, clr
  Register #(.width(32)) register_30 (.clk(clk), .Q(x23));  // open: D, en, clr
  Register #(.width(32)) register_31 (.clk(clk), .Q(x31));  // open: D, en, clr
  Multiplexer #(.enable("false"), .select(5), .width(32)) multiplexer_1 (
    .in0({32{1'b0}}), .in1(x1), .in2(x2), .in3(x3), .in4(x4), .in5(x5), .in6(x6), .in7(x7), .in8(x8),
    .in9(x9), .in10(x10), .in11(x11), .in12(x12), .in13(x13), .in14(x14), .in15(x15), .in16(x16), .in17(x17),
    .in18(x18), .in19(x19), .in20(x20), .in21(x21), .in22(x22), .in23(x23), .in24(x24), .in25(x25),
    .in26(x26), .in27(x27), .in28(x28), .in29(x29), .in30(x30), .in31(x31), .out(Read_Data_1), .sel(rs1));
  Multiplexer #(.enable("false"), .select(5), .width(32)) multiplexer_2 (
    .in0({32{1'b0}}), .in1(x1), .in2(x2), .in3(x3), .in4(x4), .in5(x5), .in6(x6), .in7(x7), .in8(x8),
    .in9(x9), .in10(x10), .in11(x11), .in12(x12), .in13(x13), .in14(x14), .in15(x15), .in16(x16), .in17(x17),
    .in18(x18), .in19(x19), .in20(x20), .in21(x21), .in22(x22), .in23(x23), .in24(x24), .in25(x25),
    .in26(x26), .in27(x27), .in28(x28), .in29(x29), .in30(x30), .in31(x31), .out(Read_Data_2), .sel(rs2));

  // Other names for the same wires on the sheet: read_data1[31:0] = Read_Data_1; read_data2[31:0] = Read_Data_2;
  //   read_reg1[4:0] = rs1; read_reg2[4:0] = rs2; write_en = RegWEn; write_reg[4:0] = rd

  // Notes on the sheet:
  //   INPUTS to your circuit
  //   DON'T CHANGE THE LOCATIONS OF THE INPUTS AND OUTPUTS!
  //   These are DEBUG/TEST outputs from your circuit.
  //   OUTPUTS from your circuit
endmodule
